# Fritzing sketch Drum Single Pad using Piezo (saved by Fritzing 0.7.11b)
breadboards: 1

parts:
  Arduino1 = Arduino
  J1 = Piezo Speaker
  R1 = Resistor [tolerance=±5% resistance=220 package=THT]

nets:
  N1: Arduino1.+5V, R1.Pin_0
  N2: Arduino1.GND, J1.pin1
  N3: Arduino1.A0, J1.pin2, R1.Pin_1
